# Fritzing sketch esp32-mpu6050 (saved by Fritzing 0.9.3b)
breadboards: 1

parts:
  U1 = ESP32S-HiLetgo [part_number=ESP32S-HiLetgo]
  Componente1 = InvenSense MPU6050
  BAT1 = BC9VPC [package=bc9vpc]

nets:
  N1: U1.3.3, Componente1.VCC
  GND: U1.GND, Componente1.GND, BAT1.V-
  N2: U1.VIN, BAT1.V+
  N3: U1.GPIO21, Componente1.SDA
  N4: U1.GPIO22, Componente1.SCL

notes:
  ESP32
  MPU6050

custom parts:
  ESP32S-HiLetgo: HiLetgo ESP-WROOM-32 ESP32 ESP-32S Development Board 2.4GHz Dual-Mode WiFi + Bluetooth Dual Cores Microcontroller The ESP32 integrated with Antenna switches, RF Balun, power amplifiers, low-noise amplifiers, filters, and management modules, and the entire solution occupies the least area of PCB. 2.4 GHz Wi-Fi plus Bluetooth dual-mode chip, with TSMC Ultra-low power consumption 40nm technology,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
